// Logisim project PipelinedMiniMIPS.circ as structural Verilog: 2 circuits, main circuit main
module main (
  input  in_1,
  input  [31:0] in_2,
  input  in_3,
  input  [4:0] in_4,
  input  [4:0] in_5,
  input  [4:0] in_6,
  output [31:0] out_7,
  output [31:0] out_8,
  output [31:0] out_9
);

  wire clock_1_out;
  wire [31:0] leftshift2_1_cou, register_1_q;

  Clock clock_1 (.out(clock_1_out));
  Register #(.width(32)) register_1 (.en(in_1), .clk(clock_1_out), .Q(register_1_q));  // open: D, clr
  // Incrementer #(.width(32)) incrementer_1: pin names not known; wires that end beside it: register_1_q
  LeftShift2 leftshift2_1 (.B(register_1_q), .Cou(leftshift2_1_cou));  // open: Cin
  // RegisterFile registerfile_1: pin names not known; wires that end beside it: in_2, clock_1_out, in_3, in_4, in_5, in_6, out_8, out_9
  // MIPSProgramROM mipsprogramrom_1: pin names not known; wires that end beside it: out_7

  // Notes on the sheet:
  //   contents of mipsprogramrom_1 (hex, n*v repeats v):
  //   ANDI $2, $1, 13
endmodule

module LeftShift2 (
  input  Cin,
  input  [31:0] B,
  output [31:0] Cou
);


  assign Cou = {B[29:0], {2{Cin}}};
endmodule
