// Logisim project mipsV4.0.circ as structural Verilog: 29 circuits, main circuit MIPS32
module MIPS32 (
  output [31:0] out_1,
  output [31:0] out_2,
  output [4:0] out_3,
  output [19:0] out_4,
  output [31:0] out_5,
  output [4:0] out_6
);

  wire adder_4_cout, and_1_out, and_2_out, branch_1_takethebranch, clock_1_out, decoding_1_immediatenotrb,
       decoding_1_isaload, decoding_1_isbranching, decoding_1_ismovn, decoding_1_ismovz, decoding_1_isstore,
       decoding_1_isunsignedslt, decoding_1_jalorjalr, decoding_1_jtype, decoding_1_mc, decoding_1_replacea,
       decoding_1_we, ex_mem_1_badaddrout, ex_mem_1_isloadout, ex_mem_1_isstoreout, ex_mem_1_jalorjalrout,
       ex_mem_1_mcout, ex_mem_1_weout, id_ex_1_isloadout, id_ex_1_isstoreout, id_ex_1_jalorjalrout,
       id_ex_1_mcout, id_ex_1_moveout, id_ex_1_rborimmout, id_ex_1_replaceaout, id_ex_1_sltunsignedout,
       id_ex_1_weout, incrementer_1_p3, load_use_hazard_detector_1_load_use_hazard, mem_wb_1_jalorjalrout,
       mem_wb_1_mcout, move_1_makemove, move_1_weoff, not_1_out, not_3_out, registerfile_1_p2;
  wire [1:0] decoding_1_replaceshamt, forwardingunit_1_forwarda, forwardingunit_1_forwardb,
       forwardra_1_forwardfrom, or_2_out;
  wire [3:0] decoding_1_aluopcode, id_ex_1_aluout;
  wire [4:0] decoding_1_ra, decoding_1_rb, decoding_1_rd, decoding_1_shamt, ex_mem_1_rdout, ex_mem_1_rwout,
       id_ex_1_raout, id_ex_1_rbout, id_ex_1_rdout, id_ex_1_rwout, id_ex_1_shamtout, jump_1_rw,
       mem_wb_1_rwout, mips_alu_1_p4, multiplexer_3_out, multiplexer_11_out, registerfile_1_p6;
  wire [15:0] branch_1_offset;
  wire [19:0] adder_4_out, bit_extender_2_out, bit_extender_3_out;
  wire [26:0] registerfile_1_p6_2;
  wire [31:0] adder_1_out, adder_2_out, adder_3_out, bit_extender_1_out, compare_1_oneifalessthanb,
       decoding_1_immediate, ex_mem_1_bout, ex_mem_1_dout, ex_mem_1_pcp8out, id_ex_1_aout, id_ex_1_bout,
       id_ex_1_immediateout, id_ex_1_pcp8out, if_id_1_iout, if_id_1_pc_out, incrementer_1_p1,
       incrementer_1_p2, jump_1_newpc, leftshift2_2_cou, mem_wb_1_dout, mips_alu_1_p5, mips_ram_1_p3,
       mipsprogramrom_1_p1, multiplexer_1_out, multiplexer_2_out, multiplexer_4_out, multiplexer_5_out,
       multiplexer_6_out, multiplexer_7_out, multiplexer_8_out, multiplexer_10_out, register_1_q,
       register_2_q, registerfile_1_p7;

  Clock clock_1 (.out(clock_1_out));
  Register #(.width(32)) register_1 (.clk(clock_1_out), .Q(register_1_q), .clr(incrementer_1_p3));  // open: D, en
  // Incrementer #(.width(32)) incrementer_1: pin names not known; wires that end beside it: incrementer_1_p1, incrementer_1_p2, incrementer_1_p3
  RightShift2 rightshift2_1 (.Bout(incrementer_1_p2), .B(multiplexer_1_out));  // open: Cin
  Multiplexer #(.select(2), .width(32), .enable("false")) multiplexer_1 (
    .in0(incrementer_1_p1), .in1(adder_1_out), .in2(adder_3_out), .in3(register_2_q),
    .out(multiplexer_1_out), .sel(or_2_out));
  Register #(.width(32)) register_2 (.D(incrementer_1_p1), .clk(clock_1_out), .Q(register_2_q));  // open: en, clr
  or or_1 (or_2_out[1], load_use_hazard_detector_1_load_use_hazard, and_1_out);
  not not_1 (not_1_out, load_use_hazard_detector_1_load_use_hazard);
  // MIPSProgramROM mipsprogramrom_1: pin names not known; wires that end beside it: mipsprogramrom_1_p1
  LeftShift2 leftshift2_1 (.B(register_1_q), .Cou(incrementer_1_p1));  // open: Cin
  or or_2 (or_2_out[0], load_use_hazard_detector_1_load_use_hazard, decoding_1_jtype);
  IF_ID if_id_1 (
    .Iout(if_id_1_iout), .ClkIn(clock_1_out), .Instruction(mipsprogramrom_1_p1), .LatchWE(not_1_out),
    .PC_In(multiplexer_1_out), .PC_Out(if_id_1_pc_out));
  // NOT_Gate not_2 has open pins: in=clock_1_out, out=open
  decoding decoding_1 (
    .ALUOpCode(decoding_1_aluopcode), .WE(decoding_1_we), .MC(decoding_1_mc), .Rb(decoding_1_rb),
    .Ra(decoding_1_ra), .immediateNotRb(decoding_1_immediatenotrb), .immediate(decoding_1_immediate),
    .replaceA(decoding_1_replacea), .Instruction(if_id_1_iout), .Rd(decoding_1_rd), .Shamt(decoding_1_shamt),
    .replaceShamt(decoding_1_replaceshamt), .isMOVN(decoding_1_ismovn), .isMOVZ(decoding_1_ismovz),
    .isUnsignedSLT(decoding_1_isunsignedslt), .jType(decoding_1_jtype), .isBranching(decoding_1_isbranching),
    .isALoad(decoding_1_isaload), .isStore(decoding_1_isstore), .JALorJALR(decoding_1_jalorjalr));  // open: constant00000
  Jump jump_1 (
    .NewPC(jump_1_newpc), .Instruction(if_id_1_iout), .OriginalPC(if_id_1_pc_out),
    .Rs_IN({registerfile_1_p6_2, registerfile_1_p6}), .rW(jump_1_rw));  // open: in_2
  Multiplexer #(.select(2), .width(32), .enable("false")) multiplexer_2 (
    .in0(jump_1_newpc), .in1(ex_mem_1_pcp8out), .in2(mem_wb_1_dout), .out(multiplexer_2_out),
    .sel(forwardra_1_forwardfrom));  // open: in3
  and and_1 (and_1_out, decoding_1_isbranching, branch_1_takethebranch);
  Branch branch_1 (
    .Instruction(if_id_1_iout), .Rs({registerfile_1_p6_2, registerfile_1_p6}), .Rt(registerfile_1_p7),
    .takeTheBranch(branch_1_takethebranch), .offset(branch_1_offset));
  // RegisterFile registerfile_1: pin names not known; wires that end beside it: out_1, registerfile_1_p2, out_3, decoding_1_ra, decoding_1_rb, {registerfile_1_p6_2, registerfile_1_p6}, registerfile_1_p7
  Adder #(.width(32)) adder_1 (.a(multiplexer_2_out), .b(32'hfffffffc), .out(adder_1_out));  // open: cin, cout
  assign bit_extender_1_out = {{16{branch_1_offset[15]}}, branch_1_offset};  // Bit_Extender bit_extender_1
  Adder #(.width(32)) adder_2 (.a(32'h8), .b(if_id_1_pc_out), .out(adder_2_out));  // open: cin, cout
  LeftShift2 leftshift2_2 (.B(bit_extender_1_out), .Cou(leftshift2_2_cou));  // open: Cin
  Adder #(.width(32)) adder_3 (.a(leftshift2_2_cou), .b(if_id_1_pc_out), .out(adder_3_out));  // open: cin, cout
  Multiplexer #(.select(2), .width(5), .enable("false")) multiplexer_3 (
    .in0(decoding_1_shamt), .in1(registerfile_1_p6), .in2(5'b10000), .out(multiplexer_3_out),
    .sel(decoding_1_replaceshamt));  // open: in3
  and and_2 (and_2_out, decoding_1_we, not_3_out);
  not not_3 (not_3_out, move_1_weoff);
  Move move_1 (
    .B(registerfile_1_p7), .MOVN(decoding_1_ismovn), .MakeMove(move_1_makemove), .MOVZ(decoding_1_ismovz),
    .WEOff(move_1_weoff));  // open: in_2
  ID_EX id_ex_1 (
    .BOut(id_ex_1_bout), .ImmediateIn(decoding_1_immediate), .ALUOut(id_ex_1_aluout),
    .RbOrImmIn(decoding_1_immediatenotrb), .ShamtIn(multiplexer_3_out), .BIn(registerfile_1_p7),
    .WEIn(and_2_out), .AOut(id_ex_1_aout), .RdIn(decoding_1_rd),
    .AIn({registerfile_1_p6_2, registerfile_1_p6}), .Clk(clock_1_out), .ShamtOut(id_ex_1_shamtout),
    .RbIn(decoding_1_rb), .RdOut(id_ex_1_rdout), .RbOrImmOut(id_ex_1_rborimmout), .RaOut(id_ex_1_raout),
    .ImmediateOut(id_ex_1_immediateout), .ALUIn(decoding_1_aluopcode), .RaIn(decoding_1_ra),
    .RbOut(id_ex_1_rbout), .WEOut(id_ex_1_weout), .MCIn(decoding_1_mc), .MCOut(id_ex_1_mcout),
    .MoveIn(move_1_makemove), .MoveOut(id_ex_1_moveout), .sltunsignIn(decoding_1_isunsignedslt),
    .sltunsignedOut(id_ex_1_sltunsignedout), .replaceAIn(decoding_1_replacea),
    .replaceAOut(id_ex_1_replaceaout), .LatchWE(not_1_out), .isLoad(decoding_1_isaload),
    .isStore(decoding_1_isstore), .isLoadOut(id_ex_1_isloadout), .isStoreOut(id_ex_1_isstoreout),
    .JALorJALRin(decoding_1_jalorjalr), .JALorJALRout(id_ex_1_jalorjalrout), .rWin(jump_1_rw),
    .rWout(id_ex_1_rwout), .pcp8in(adder_2_out), .pcp8out(id_ex_1_pcp8out));
  Multiplexer #(.width(32), .enable("false")) multiplexer_4 (
    .in0(id_ex_1_bout), .in1(id_ex_1_aout), .out(multiplexer_4_out), .sel(id_ex_1_moveout));
  forwardRA forwardra_1 (
    .rW_WB(mem_wb_1_rwout), .isJALorJALR_WB(mem_wb_1_jalorjalrout), .rW_MEM(ex_mem_1_rwout),
    .isJALorJALR_MEM(ex_mem_1_jalorjalrout), .instruction(if_id_1_iout), .forwardFrom(forwardra_1_forwardfrom));
  Multiplexer #(.select(2), .width(32), .enable("false")) multiplexer_5 (
    .in0(id_ex_1_aout), .in1(out_1), .in2(ex_mem_1_dout), .out(multiplexer_5_out),
    .sel(forwardingunit_1_forwarda));  // open: in3
  Multiplexer #(.select(2), .width(32), .enable("false")) multiplexer_6 (
    .in0(multiplexer_4_out), .in1(out_1), .in2(ex_mem_1_dout), .out(multiplexer_6_out),
    .sel(forwardingunit_1_forwardb));  // open: in3
  compare compare_1 (
    .A(multiplexer_5_out), .oneIfALessThanB(compare_1_oneifalessthanb), .B(multiplexer_7_out),
    .isUnsigned(id_ex_1_sltunsignedout));
  Multiplexer #(.width(32), .enable("false")) multiplexer_7 (
    .in0(multiplexer_6_out), .in1(id_ex_1_immediateout), .out(multiplexer_7_out), .sel(id_ex_1_rborimmout));
  forwardingUnit forwardingunit_1 (
    .ID_EX_Rs(id_ex_1_raout), .ID_EX_Rt(id_ex_1_rbout), .EX_MEM_Rd(ex_mem_1_rdout),
    .EX_MEM_WE(ex_mem_1_weout), .MEM_WB_Rd(out_3), .MEM_WB_WE(registerfile_1_p2),
    .ForwardA(forwardingunit_1_forwarda), .ForwardB(forwardingunit_1_forwardb));
  Multiplexer #(.width(32), .enable("false")) multiplexer_8 (
    .in0(multiplexer_5_out), .in1(compare_1_oneifalessthanb), .out(multiplexer_8_out),
    .sel(id_ex_1_replaceaout));
  // Mips_ALU mips_alu_1: pin names not known; wires that end beside it: multiplexer_8_out, multiplexer_7_out, id_ex_1_aluout, mips_alu_1_p4, mips_alu_1_p5
  Multiplexer #(.select(2), .width(5), .enable("false")) multiplexer_9 (
    .in0(id_ex_1_shamtout), .in1(out_1[4:0]), .in2(ex_mem_1_dout[4:0]), .out(mips_alu_1_p4),
    .sel(forwardingunit_1_forwarda));  // open: in3
  Bit_Extender #(.in_width(32), .out_width(20)) bit_extender_2 (.in(multiplexer_5_out), .out(bit_extender_2_out));
  Bit_Extender #(.in_width(32), .out_width(20)) bit_extender_3 (.in(id_ex_1_immediateout), .out(bit_extender_3_out));
  Adder #(.width(20)) adder_4 (
    .a(bit_extender_2_out), .b(bit_extender_3_out), .out(adder_4_out), .cout(adder_4_cout));  // open: cin
  Load_Use_Hazard_Detector load_use_hazard_detector_1 (
    .Load_Use_Hazard(load_use_hazard_detector_1_load_use_hazard), .IDEX_Rd(id_ex_1_rdout),
    .IFID_Ra(decoding_1_ra), .IDEX_MemRead(id_ex_1_mcout), .IFID_Rb(decoding_1_rb));
  EX_MEM ex_mem_1 (
    .Clk(clock_1_out), .DOut(ex_mem_1_dout), .DIn(mips_alu_1_p5), .WEIn(id_ex_1_weout),
    .WEOut(ex_mem_1_weout), .RdOut(ex_mem_1_rdout), .BOut(ex_mem_1_bout), .RdIn(id_ex_1_rdout),
    .BIn(multiplexer_7_out), .MCIn(id_ex_1_mcout), .MCOut(ex_mem_1_mcout), .isStore(id_ex_1_isstoreout),
    .isLoad(id_ex_1_isloadout), .isLoadOut(ex_mem_1_isloadout), .isStoreOut(ex_mem_1_isstoreout),
    .MemAddr(adder_4_out), .MemAddrOut(out_4), .BadAddr(adder_4_cout), .BadAddrOut(ex_mem_1_badaddrout),
    .JALorJALRin(id_ex_1_jalorjalrout), .JALorJALRout(ex_mem_1_jalorjalrout), .rWin(id_ex_1_rwout),
    .rWout(ex_mem_1_rwout), .pcp8in(id_ex_1_pcp8out), .pcp8out(ex_mem_1_pcp8out),
    .PassBubble(load_use_hazard_detector_1_load_use_hazard));
  // AND_Gate and_3 has open pins: in0=ex_mem_1_isstoreout, in1=ex_mem_1_badaddrout, out=open
  // MIPS_RAM mips_ram_1: pin names not known; wires that end beside it: ex_mem_1_bout, clock_1_out, mips_ram_1_p3
  // AND_Gate and_4 has open pins: in0=ex_mem_1_isloadout, in1=ex_mem_1_badaddrout, out=open
  Multiplexer #(.width(32), .enable("false")) multiplexer_10 (
    .in0(ex_mem_1_dout), .in1(ex_mem_1_pcp8out), .out(multiplexer_10_out), .sel(ex_mem_1_jalorjalrout));
  Multiplexer #(.width(5), .enable("false")) multiplexer_11 (
    .in0(ex_mem_1_rdout), .in1(ex_mem_1_rwout), .out(multiplexer_11_out), .sel(ex_mem_1_jalorjalrout));
  MEM_WB mem_wb_1 (
    .DOut(mem_wb_1_dout), .Clk(clock_1_out), .MOut(out_5), .WEIn(ex_mem_1_weout), .MIn(mips_ram_1_p3),
    .WEOut(registerfile_1_p2), .RdOut(out_3), .Rd(multiplexer_11_out), .DIn(multiplexer_10_out),
    .MCIn(ex_mem_1_mcout), .MCOut(mem_wb_1_mcout), .JALorJALRin(ex_mem_1_jalorjalrout),
    .JALorJALRout(mem_wb_1_jalorjalrout), .rWin(ex_mem_1_rwout), .rWout(mem_wb_1_rwout));
  Multiplexer #(.width(32), .enable("false")) multiplexer_12 (
    .in0(mem_wb_1_dout), .in1(out_5), .out(out_1), .sel(mem_wb_1_mcout));

  assign out_2 = out_1;
  assign out_6 = out_3;

  // Notes on the sheet:
  //   contents of mipsprogramrom_1 (hex, n*v repeats v):
  //   ADDIU $2, $2, 2  ADDIU $3, $3, 3  ADDIU $4, $4, 4  ADDIU $5, $5, 5  ADDIU $6, $6, 6  ADDIU $7, $7, 7
  //   ADDIU $8, $8, 4  ADDIU $9, $9, 2048  SW $9, 3($8)  LW $12, 3($8)  LW $10, 3($8)  ADDIU $11, $10, 9
  //   JAL 0 ADDIU $15, $15, 16
endmodule

module LeftShift2 (
  input  Cin,
  input  [31:0] B,
  output [31:0] Cou
);


  assign Cou = {B[29:0], {2{Cin}}};
endmodule

module IF_ID (
  input  LatchWE,
  input  [31:0] Instruction,
  input  [31:0] PC_In,
  input  ClkIn,
  output [31:0] Iout,
  output [31:0] PC_Out
);

  Register #(.width(32)) PCIn (.D(PC_In), .en(LatchWE), .clk(ClkIn), .Q(PC_Out));  // open: clr
  Register #(.width(32)) rIn (.D(Instruction), .en(LatchWE), .clk(ClkIn), .Q(Iout));  // open: clr
endmodule

module ID_EX (
  input  LatchWE,
  input  [31:0] AIn,
  input  [31:0] BIn,
  input  [31:0] ImmediateIn,
  input  [4:0] RaIn,
  input  [4:0] RbIn,
  input  [4:0] RdIn,
  input  [4:0] ShamtIn,
  input  [3:0] ALUIn,
  input  WEIn,
  input  RbOrImmIn,
  input  replaceAIn,
  input  MCIn,
  input  MoveIn,
  input  Clk,
  input  sltunsignIn,
  input  isLoad,
  input  isStore,
  input  JALorJALRin,
  input  [4:0] rWin,
  input  [31:0] pcp8in,
  output [31:0] AOut,
  output [4:0] RaOut,
  output [31:0] BOut,
  output [4:0] RbOut,
  output [4:0] RdOut,
  output [31:0] ImmediateOut,
  output [4:0] ShamtOut,
  output [3:0] ALUOut,
  output WEOut,
  output RbOrImmOut,
  output replaceAOut,
  output MCOut,
  output MoveOut,
  output sltunsignedOut,
  output isLoadOut,
  output isStoreOut,
  output JALorJALRout,
  output [4:0] rWout,
  output [31:0] pcp8out
);

  Register #(.width(32)) register_1 (.D(AIn), .en(LatchWE), .clk(Clk), .Q(AOut));  // open: clr
  Register #(.width(1)) register_2 (.D(MCIn), .en(Clk), .clk(Clk), .Q(MCOut));  // open: clr
  Register #(.width(32)) register_3 (.D(BIn), .en(LatchWE), .clk(Clk), .Q(BOut));  // open: clr
  Register #(.width(1)) register_4 (.D(isLoad), .en(Clk), .clk(Clk), .Q(isLoadOut));  // open: clr
  Register #(.width(4)) register_5 (.D(ALUIn), .en(Clk), .clk(Clk), .Q(ALUOut));  // open: clr
  Register #(.width(1)) register_6 (.D(isStore), .en(Clk), .clk(Clk), .Q(isStoreOut));  // open: clr
  Register #(.width(32)) register_7 (.D(ImmediateIn), .en(LatchWE), .clk(Clk), .Q(ImmediateOut));  // open: clr
  Register #(.width(1)) register_8 (.D(WEIn), .en(Clk), .clk(Clk), .Q(WEOut));  // open: clr
  Register #(.width(5)) register_9 (.D(RaIn), .en(LatchWE), .clk(Clk), .Q(RaOut));  // open: clr
  Register #(.width(1)) register_10 (.D(RbOrImmIn), .en(Clk), .clk(Clk), .Q(RbOrImmOut));  // open: clr
  Register #(.width(1)) register_11 (.D(MoveIn), .en(Clk), .clk(Clk), .Q(MoveOut));  // open: clr
  Register #(.width(5)) register_12 (.D(RbIn), .en(LatchWE), .clk(Clk), .Q(RbOut));  // open: clr
  Register #(.width(1)) register_13 (.D(replaceAIn), .en(Clk), .clk(Clk), .Q(replaceAOut));  // open: clr
  Register #(.width(1)) register_14 (.D(sltunsignIn), .en(Clk), .clk(Clk), .Q(sltunsignedOut));  // open: clr
  Register #(.width(1)) register_15 (.D(JALorJALRin), .en(Clk), .clk(Clk), .Q(JALorJALRout));  // open: clr
  Register #(.width(5)) register_16 (.D(rWin), .en(Clk), .clk(Clk), .Q(rWout));  // open: clr
  Register #(.width(32)) register_17 (.D(pcp8in), .en(Clk), .clk(Clk), .Q(pcp8out));  // open: clr
  Register #(.width(5)) register_18 (.D(RdIn), .en(LatchWE), .clk(Clk), .Q(RdOut));  // open: clr
  Register #(.width(5)) register_19 (.D(ShamtIn), .en(LatchWE), .clk(Clk), .Q(ShamtOut));  // open: clr
endmodule

module decoding (
  input  [4:0] constant00000,
  input  [31:0] Instruction,
  output [3:0] ALUOpCode,
  output [4:0] Ra,
  output [4:0] Rb,
  output [4:0] Rd,
  output [4:0] Shamt,
  output jType,
  output [1:0] replaceShamt,
  output WE,
  output [31:0] immediate,
  output replaceA,
  output immediateNotRb,
  output MC,
  output isMOVN,
  output isMOVZ,
  output isUnsignedSLT,
  output isBranching,
  output isALoad,
  output isStore,
  output JALorJALR
);

  wire and_2_out, and_3_out, and_4_out, and_5_out, and_6_out, and_7_out, and_8_out, isbeqorbne_1_isbneorbeq,
       isjorjr_1_jorjr, not_1_out, not_2_out, not_3_out, not_4_out, not_5_out, not_6_out, not_7_out,
       not_8_out, not_9_out, not_10_out, not_11_out, not_12_out, not_13_out, not_14_out, not_15_out,
       not_16_out, not_17_out, or_1_out, or_2_out, or_3_out, or_4_out, or_6_out;
  wire [15:0] bit_extender_1_out;

  not not_1 (not_1_out, Instruction[31]);
  not not_2 (not_2_out, Instruction[30]);
  not not_3 (not_3_out, Instruction[29]);
  not not_4 (not_4_out, Instruction[28]);
  not not_5 (not_5_out, Instruction[27]);
  not not_6 (not_6_out, Instruction[3]);
  not not_7 (not_7_out, Instruction[31]);
  and and_1 (immediateNotRb, not_7_out, not_8_out, Instruction[29]);
  not not_8 (not_8_out, Instruction[30]);
  and and_2 (and_2_out, not_1_out, not_2_out, not_3_out, not_4_out, not_5_out, Instruction[26]);
  or or_1 (or_1_out, Instruction[5], Instruction[4], not_6_out, Instruction[2], Instruction[1]);
  or or_2 (or_2_out, immediateNotRb, Instruction[31]);
  or or_3 (or_3_out, Instruction[31], Instruction[30], Instruction[29], Instruction[28], Instruction[27], Instruction[26]);
  not not_9 (not_9_out, or_3_out);
  not not_10 (not_10_out, Instruction[31]);
  not not_11 (not_11_out, Instruction[30]);
  and and_3 (and_3_out, not_10_out, not_11_out, Instruction[29], not_12_out);
  not not_12 (not_12_out, Instruction[28]);
  not not_13 (not_13_out, Instruction[31]);
  not not_14 (not_14_out, Instruction[30]);
  and and_4 (and_4_out, not_13_out, not_14_out, not_15_out, Instruction[28]);
  not not_15 (not_15_out, Instruction[29]);
  and and_5 (and_5_out, not_9_out, or_1_out);
  not not_16 (not_16_out, Instruction[5]);
  assign bit_extender_1_out = {{15{Instruction[15]}}, Instruction[15]};  // Bit_Extender bit_extender_1
  not not_17 (not_17_out, Instruction[28]);
  // Probe on or_2_out
  // Probe on and_5_out
  or or_4 (or_4_out, and_2_out, Instruction[31], and_3_out, and_4_out);
  and and_6 (and_6_out, or_2_out, Instruction[29], not_17_out, Instruction[27]);
  and and_7 (and_7_out, and_5_out, Instruction[3], Instruction[5]);
  isJType isjtype_1 (.opcode(Instruction[31:26]), .funct(Instruction[5:0]), .jType(jType));
  Multiplexer #(.width(32), .enable("false")) multiplexer_1 (
    .in0({{16{1'b0}}, Instruction[15:0]}), .in1({bit_extender_1_out, Instruction[15:0]}), .out(immediate),
    .sel(or_4_out));
  isBEQorBNE isbeqorbne_1 (.opode(Instruction[31:26]), .isBNEorBEQ(isbeqorbne_1_isbneorbeq));
  and and_8 (and_8_out, and_5_out, ~Instruction[31]);  // AND_Gate
  or or_5 (replaceA, and_6_out, and_7_out);
  or or_6 (or_6_out, Instruction[31], isbeqorbne_1_isbneorbeq, and_5_out);
  Multiplexer #(.width(5), .enable("false")) multiplexer_2 (
    .in0(Instruction[20:16]), .in1(Instruction[15:11]), .out(Rd), .sel(and_8_out));
  Multiplexer #(.width(5), .enable("false")) multiplexer_3 (
    .in0({5{1'b0}}), .in1(Instruction[10:6]), .out(Shamt), .sel(or_6_out));
  isJorJR isjorjr_1 (.opcode(Instruction[31:26]), .funct(Instruction[5:0]), .JorJR(isjorjr_1_jorjr));
  nor nor_1 (WE, isjorjr_1_jorjr, isStore, isBranching);
  generateOpcode generateopcode_1 (.sixBitOpCode(Instruction[31:26]), .funct(Instruction[5:0]), .ALUOpCode(ALUOpCode));
  Multiplexer #(.width(5), .enable("false")) multiplexer_4 (
    .in0(constant00000), .in1(Instruction[20:16]), .out(Rb), .sel(or_6_out));
  and and_9 (replaceShamt[0], Instruction[2], not_16_out, and_5_out);
  isStore1 isstore1_1 (.opcode(Instruction[31:26]), .isStore(isStore));
  isLUI islui_1 (.opcode(Instruction[31:26]), .LUI(replaceShamt[1]));
  isMOVN_MOVZ ismovn_movz_1 (.opcode(Instruction[31:26]), .funct(Instruction[5:0]), .MOVN(isMOVN), .MOVZ(isMOVZ));
  isBranchingOrNot isbranchingornot_1 (.sixBitOpcode(Instruction[31:26]), .isBranching(isBranching));
  isLoad isload_1 (.opcode(Instruction[31:26]), .isLoad(isALoad));
  isJALorJALR isjalorjalr_1 (.opcode(Instruction[31:26]), .funct(Instruction[5:0]), .JALorJALR(JALorJALR));
  sltunsigned sltunsigned_1 (.opcode(Instruction[31:26]), .funct(Instruction[5:0]), .itIsUnsigned(isUnsignedSLT));

  assign MC = Instruction[31];
  assign Ra = Instruction[25:21];
endmodule

module generateOpcode (
  input  [5:0] sixBitOpCode,
  input  [5:0] funct,
  output [3:0] ALUOpCode
);

  wire not_1_out, or_1_out;
  wire [3:0] generateopcode2_1_a0, generateopcode3_1_a0;

  or or_1 (or_1_out, sixBitOpCode[0], sixBitOpCode[1], sixBitOpCode[2], sixBitOpCode[3], sixBitOpCode[4], sixBitOpCode[5]);
  not not_1 (not_1_out, or_1_out);
  generateOpcode2 generateopcode2_1 (
    .f5(funct[5]), .f4(funct[4]), .f3(funct[3]), .f2(funct[2]), .f1(funct[1]), .f0(funct[0]),
    .a3(generateopcode2_1_a0[3]), .a2(generateopcode2_1_a0[2]), .a1(generateopcode2_1_a0[1]),
    .a0(generateopcode2_1_a0[0]));
  generateOpcode3 generateopcode3_1 (
    .sb5(sixBitOpCode[5]), .sb4(sixBitOpCode[4]), .sb3(sixBitOpCode[3]), .sb2(sixBitOpCode[2]),
    .sb1(sixBitOpCode[1]), .sb0(sixBitOpCode[0]), .a3(generateopcode3_1_a0[3]), .a2(generateopcode3_1_a0[2]),
    .a1(generateopcode3_1_a0[1]), .a0(generateopcode3_1_a0[0]));
  Multiplexer #(.width(4), .enable("false")) multiplexer_1 (
    .in0(generateopcode3_1_a0), .in1(generateopcode2_1_a0), .out(ALUOpCode), .sel(not_1_out));
endmodule

module generateOpcode2 (
  input  f5,
  input  f4,
  input  f3,
  input  f2,
  input  f1,
  input  f0,
  output a3,
  output a2,
  output a1,
  output a0
);

  wire and_1_out, and_2_out, and_3_out, and_4_out, and_5_out, and_6_out, and_7_out, and_8_out, not_1_out,
       not_2_out, not_3_out, not_4_out, not_5_out, not_6_out, not_7_out, not_8_out;

  and and_1 (and_1_out, f5, f2);
  not not_1 (not_1_out, f3);
  not not_2 (not_2_out, f5);
  not not_3 (not_3_out, f3);
  not not_4 (not_4_out, f2);
  not not_5 (not_5_out, f3);
  not not_6 (not_6_out, f5);
  not not_7 (not_7_out, f3);
  not not_8 (not_8_out, f2);
  or or_1 (a3, f3, and_1_out);
  and and_2 (and_2_out, not_1_out, f1);
  and and_3 (and_3_out, f5, f1);
  and and_4 (and_4_out, not_2_out, f3);
  and and_5 (and_5_out, f5, not_3_out, not_4_out);
  and and_6 (and_6_out, f5, not_5_out, f0);
  and and_7 (and_7_out, not_6_out, not_7_out, f0);
  and and_8 (and_8_out, f5, not_8_out);
  or or_2 (a2, and_2_out, and_3_out);
  or or_3 (a1, and_4_out, and_5_out, and_6_out);
  or or_4 (a0, and_7_out, and_8_out);
endmodule

module generateOpcode3 (
  input  sb5,
  input  sb4,
  input  sb3,
  input  sb2,
  input  sb1,
  input  sb0,
  output a3,
  output a2,
  output a1,
  output a0
);

  wire and_1_out, and_2_out, and_3_out, and_4_out, not_1_out, not_2_out, not_3_out, not_4_out, not_5_out,
       not_7_out;

  not not_1 (not_1_out, sb2);
  not not_2 (not_2_out, sb1);
  not not_3 (not_3_out, sb2);
  not not_4 (not_4_out, sb0);
  not not_5 (not_5_out, sb1);
  not not_6 (a0, sb2);
  not not_7 (not_7_out, sb0);
  and and_1 (and_1_out, not_1_out, sb1);
  and and_2 (and_2_out, sb2, not_2_out);
  and and_3 (and_3_out, not_3_out, sb1);
  and and_4 (and_4_out, sb1, not_4_out);
  and and_5 (a1, not_5_out, sb0);
  or or_1 (a3, not_7_out, and_1_out, and_2_out);
  or or_2 (a2, and_3_out, and_4_out);
endmodule

module EX_MEM (
  input  PassBubble,
  input  [31:0] DIn,
  input  [31:0] BIn,
  input  [4:0] RdIn,
  input  WEIn,
  input  MCIn,
  input  Clk,
  input  isLoad,
  input  isStore,
  input  [19:0] MemAddr,
  input  BadAddr,
  input  JALorJALRin,
  input  [4:0] rWin,
  input  [31:0] pcp8in,
  output [31:0] DOut,
  output [31:0] BOut,
  output [4:0] RdOut,
  output WEOut,
  output MCOut,
  output isLoadOut,
  output isStoreOut,
  output [19:0] MemAddrOut,
  output BadAddrOut,
  output JALorJALRout,
  output [4:0] rWout,
  output [31:0] pcp8out
);

  wire and_1_out, and_2_out, and_3_out, and_4_out, and_8_out, and_9_out, not_1_out, register_1_q;
  wire [4:0] and_7_out, and_11_out, bit_extender_2_out, bit_extender_4_out;
  wire [19:0] and_10_out, bit_extender_3_out;
  wire [31:0] and_5_out, and_6_out, and_12_out, bit_extender_1_out, bit_extender_5_out;

  Register #(.width(1)) register_1 (.D(not_1_out), .clk(Clk), .Q(register_1_q));  // open: en, clr
  not not_1 (not_1_out, PassBubble);
  assign bit_extender_1_out = {{31{register_1_q}}, register_1_q};  // Bit_Extender bit_extender_1
  assign bit_extender_2_out = {{4{register_1_q}}, register_1_q};  // Bit_Extender bit_extender_2
  and and_1 (and_1_out, register_1_q, isLoad);
  and and_2 (and_2_out, register_1_q, isStore);
  assign bit_extender_3_out = {{19{register_1_q}}, register_1_q};  // Bit_Extender bit_extender_3
  and and_3 (and_3_out, register_1_q, BadAddr);
  and and_4 (and_4_out, register_1_q, JALorJALRin);
  assign bit_extender_4_out = {{4{register_1_q}}, register_1_q};  // Bit_Extender bit_extender_4
  assign bit_extender_5_out = {{31{register_1_q}}, register_1_q};  // Bit_Extender bit_extender_5
  assign and_5_out = bit_extender_1_out & DIn;  // AND_Gate and_5, 32 bits wide
  Register #(.width(32)) register_2 (.D(and_5_out), .clk(Clk), .Q(DOut));  // open: en, clr
  assign and_6_out = bit_extender_1_out & BIn;  // AND_Gate and_6, 32 bits wide
  assign and_7_out = bit_extender_2_out & RdIn;  // AND_Gate and_7, 5 bits wide
  and and_8 (and_8_out, register_1_q, WEIn);
  and and_9 (and_9_out, register_1_q, MCIn);
  Register #(.width(1)) register_3 (.D(and_1_out), .clk(Clk), .Q(isLoadOut));  // open: en, clr
  Register #(.width(20)) register_4 (.D(and_10_out), .clk(Clk), .Q(MemAddrOut));  // open: en, clr
  assign and_10_out = bit_extender_3_out & MemAddr;  // AND_Gate and_10, 20 bits wide
  assign and_11_out = bit_extender_4_out & rWin;  // AND_Gate and_11, 5 bits wide
  assign and_12_out = bit_extender_5_out & pcp8in;  // AND_Gate and_12, 32 bits wide
  Register #(.width(32)) register_5 (.D(and_6_out), .clk(Clk), .Q(BOut));  // open: en, clr
  Register #(.width(1)) register_6 (.D(and_2_out), .clk(Clk), .Q(isStoreOut));  // open: en, clr
  Register #(.width(1)) register_7 (.D(and_3_out), .clk(Clk), .Q(BadAddrOut));  // open: en, clr
  Register #(.width(1)) register_8 (.D(and_4_out), .clk(Clk), .Q(JALorJALRout));  // open: en, clr
  Register #(.width(5)) register_9 (.D(and_11_out), .clk(Clk), .Q(rWout));  // open: en, clr
  Register #(.width(32)) register_10 (.D(and_12_out), .clk(Clk), .Q(pcp8out));  // open: en, clr
  Register #(.width(5)) register_11 (.D(and_7_out), .clk(Clk), .Q(RdOut));  // open: en, clr
  Register #(.width(1)) register_12 (.D(and_8_out), .clk(Clk), .Q(WEOut));  // open: en, clr
  Register #(.width(1)) register_13 (.D(and_9_out), .clk(Clk), .Q(MCOut));  // open: en, clr
endmodule

module MEM_WB (
  input  [31:0] DIn,
  input  [31:0] MIn,
  input  [4:0] Rd,
  input  WEIn,
  input  MCIn,
  input  JALorJALRin,
  input  Clk,
  input  [4:0] rWin,
  output [31:0] DOut,
  output [31:0] MOut,
  output [4:0] RdOut,
  output WEOut,
  output MCOut,
  output JALorJALRout,
  output [4:0] rWout
);

  Register #(.width(32)) register_1 (.D(DIn), .clk(Clk), .Q(DOut));  // open: en, clr
  Register #(.width(32)) register_2 (.D(MIn), .clk(Clk), .Q(MOut));  // open: en, clr
  Register #(.width(5)) register_3 (.D(Rd), .clk(Clk), .Q(RdOut));  // open: en, clr
  Register #(.width(1)) register_4 (.D(WEIn), .clk(Clk), .Q(WEOut));  // open: en, clr
  Register #(.width(1)) register_5 (.D(MCIn), .clk(Clk), .Q(MCOut));  // open: en, clr
  Register #(.width(1)) register_6 (.D(JALorJALRin), .clk(Clk), .Q(JALorJALRout));  // open: en, clr
  Register #(.width(5)) register_7 (.D(rWin), .clk(Clk), .Q(rWout));  // open: en, clr
endmodule

module forwardingUnit (
  input  [4:0] ID_EX_Rs,
  input  [4:0] ID_EX_Rt,
  input  [4:0] EX_MEM_Rd,
  input  EX_MEM_WE,
  input  [4:0] MEM_WB_Rd,
  input  MEM_WB_WE,
  output [1:0] ForwardA,
  output [1:0] ForwardB
);

  wire not_1_out, not_2_out, not_3_out, not_4_out, not_5_out, not_6_out, or_1_out, or_2_out, or_3_out,
       or_4_out, or_5_out, or_6_out;
  wire [4:0] xor_1_out, xor_2_out, xor_3_out, xor_4_out;

  or or_1 (or_1_out, EX_MEM_Rd[0], EX_MEM_Rd[1], EX_MEM_Rd[2], EX_MEM_Rd[3], EX_MEM_Rd[4]);
  or or_2 (or_2_out, MEM_WB_Rd[0], MEM_WB_Rd[1], MEM_WB_Rd[2], MEM_WB_Rd[3], MEM_WB_Rd[4]);
  assign xor_1_out = ID_EX_Rs ^ EX_MEM_Rd;  // XOR_Gate xor_1, 5 bits wide
  or or_3 (or_3_out, xor_1_out[0], xor_1_out[1], xor_1_out[2], xor_1_out[3], xor_1_out[4]);
  not not_1 (not_1_out, or_3_out);
  assign xor_2_out = ID_EX_Rt ^ EX_MEM_Rd;  // XOR_Gate xor_2, 5 bits wide
  assign xor_3_out = ID_EX_Rs ^ MEM_WB_Rd;  // XOR_Gate xor_3, 5 bits wide
  and and_1 (ForwardA[1], not_1_out, or_1_out, EX_MEM_WE);
  or or_4 (or_4_out, xor_2_out[0], xor_2_out[1], xor_2_out[2], xor_2_out[3], xor_2_out[4]);
  not not_2 (not_2_out, or_4_out);
  or or_5 (or_5_out, xor_3_out[0], xor_3_out[1], xor_3_out[2], xor_3_out[3], xor_3_out[4]);
  not not_3 (not_3_out, ForwardA[1]);
  assign xor_4_out = ID_EX_Rt ^ MEM_WB_Rd;  // XOR_Gate xor_4, 5 bits wide
  and and_2 (ForwardB[1], not_2_out, or_1_out, EX_MEM_WE);
  and and_3 (ForwardA[0], MEM_WB_WE, or_2_out, not_4_out, not_3_out);
  not not_4 (not_4_out, or_5_out);
  or or_6 (or_6_out, xor_4_out[0], xor_4_out[1], xor_4_out[2], xor_4_out[3], xor_4_out[4]);
  not not_5 (not_5_out, ForwardB[1]);
  and and_4 (ForwardB[0], MEM_WB_WE, or_2_out, not_6_out, not_5_out);
  not not_6 (not_6_out, or_6_out);
endmodule

module isJType (
  input  [5:0] opcode,
  input  [5:0] funct,
  output jType
);

  wire and_1_out, and_2_out, not_1_out, not_2_out, not_3_out, not_4_out, not_5_out, not_6_out, not_7_out,
       or_1_out, or_2_out;

  not not_1 (not_1_out, funct[3]);
  or or_1 (or_1_out, opcode[0], opcode[1], opcode[2], opcode[3], opcode[4], opcode[5]);
  or or_2 (or_2_out, funct[5], funct[4], not_1_out, funct[2], funct[1]);
  not not_2 (not_2_out, or_2_out);
  not not_3 (not_3_out, or_1_out);
  not not_4 (not_4_out, opcode[5]);
  not not_5 (not_5_out, opcode[4]);
  not not_6 (not_6_out, opcode[3]);
  not not_7 (not_7_out, opcode[2]);
  and and_1 (and_1_out, not_3_out, not_2_out);
  and and_2 (and_2_out, not_4_out, not_5_out, not_6_out, not_7_out, opcode[1]);
  or or_3 (jType, and_2_out, and_1_out);
endmodule

module isLUI (
  input  [5:0] opcode,
  output LUI
);

  wire not_1_out, not_2_out;

  not not_1 (not_1_out, opcode[5]);
  not not_2 (not_2_out, opcode[4]);
  and and_1 (LUI, not_1_out, not_2_out, opcode[3], opcode[2], opcode[1], opcode[0]);
endmodule

module isMOVN_MOVZ (
  input  [5:0] opcode,
  input  [5:0] funct,
  output MOVN,
  output MOVZ
);

  wire not_1_out, not_2_out, not_3_out, not_4_out, not_5_out, not_6_out, not_7_out, not_8_out, or_1_out,
       or_2_out, or_3_out;

  not not_1 (not_1_out, funct[0]);
  not not_2 (not_2_out, funct[1]);
  not not_3 (not_3_out, funct[3]);
  not not_4 (not_4_out, funct[1]);
  not not_5 (not_5_out, funct[3]);
  not not_6 (not_6_out, or_1_out);
  or or_1 (or_1_out, opcode[0], opcode[1], opcode[2], opcode[3], opcode[4], opcode[5]);
  not not_7 (not_7_out, or_2_out);
  or or_2 (or_2_out, not_1_out, not_2_out, funct[2], not_3_out, funct[4], funct[5]);
  or or_3 (or_3_out, funct[0], not_4_out, funct[2], not_5_out, funct[4], funct[5]);
  not not_8 (not_8_out, or_3_out);
  and and_1 (MOVN, not_6_out, not_7_out);
  and and_2 (MOVZ, not_6_out, not_8_out);
endmodule

module Move (
  input  [31:0] B,
  input  in_2,
  input  MOVN,
  input  MOVZ,
  output MakeMove,
  output WEOff
);

  wire and_1_out, and_2_out, comparator_1_eq, not_1_out, not_2_out, or_2_out;
  wire [31:0] bit_extender_1_out;

  assign bit_extender_1_out = {{31{in_2}}, in_2};  // Bit_Extender bit_extender_1
  Comparator #(.width(32)) comparator_1 (.a(B), .b(bit_extender_1_out), .eq(comparator_1_eq));  // open: gt, lt
  not not_1 (not_1_out, comparator_1_eq);
  and and_1 (and_1_out, comparator_1_eq, MOVZ);
  and and_2 (and_2_out, not_1_out, MOVN);
  or or_1 (MakeMove, and_1_out, and_2_out);
  or or_2 (or_2_out, MOVN, MOVZ);
  not not_2 (not_2_out, MakeMove);
  and and_3 (WEOff, not_2_out, or_2_out);
endmodule

module LCD_Screen_Decode (
  input  [31:0] Instruction,
  output [6:0] RtXcord,
  output [15:0] RBG,
  output [6:0] RsYCord,
  output WE
);

  wire and_1_out, not_2_out, not_3_out, not_4_out, not_5_out;
  wire [0:0] not_6_out;
  wire [1:1] not_1_out;

  not not_1 (not_1_out[1], Instruction[26]);
  not not_2 (not_2_out, Instruction[27]);
  not not_3 (not_3_out, Instruction[29]);
  not not_4 (not_4_out, Instruction[30]);
  not not_5 (not_5_out, Instruction[31]);
  Multiplexer #(.width(2), .enable("false")) multiplexer_1 (
    .in0({Instruction[29], Instruction[27]}), .in1({not_1_out[1], Instruction[26]}), .out(RtXcord[6:5]),
    .sel(and_1_out));
  not not_6 (not_6_out[0], Instruction[26]);
  and and_1 (and_1_out, not_2_out, Instruction[28], not_3_out, not_4_out, not_5_out);
  Multiplexer #(.width(2), .enable("false")) multiplexer_2 (
    .in0({Instruction[29], Instruction[27]}), .in1({Instruction[26], not_6_out[0]}), .out(RsYCord[6:5]),
    .sel(and_1_out));
  or or_1 (WE, Instruction[31], and_1_out);

  assign RBG = Instruction[15:0];
  assign RsYCord[4:0] = Instruction[25:21];
  assign RtXcord[4:0] = Instruction[20:16];
endmodule

module compare (
  input  [31:0] A,
  input  [31:0] B,
  input  isUnsigned,
  output [31:0] oneIfALessThanB
);

  wire comparator_1_gt, comparator_2_gt, multiplexer_1_out;

  Comparator #(.width(32)) comparator_1 (.a(B), .b(A), .gt(comparator_1_gt));  // open: eq, lt
  Comparator #(.width(32), .mode("unsigned")) comparator_2 (.a(B), .b(A), .gt(comparator_2_gt));  // open: eq, lt
  Multiplexer #(.enable("false")) multiplexer_1 (
    .in0(comparator_1_gt), .in1(comparator_2_gt), .out(multiplexer_1_out), .sel(isUnsigned));
  assign oneIfALessThanB = {{31{1'b0}}, multiplexer_1_out};  // Bit_Extender bit_extender_1
endmodule

module sltunsigned (
  input  [5:0] opcode,
  input  [5:0] funct,
  output itIsUnsigned
);

  wire and_1_out, and_2_out, not_1_out, not_2_out, or_1_out;

  not not_1 (not_1_out, not_2_out);
  or or_1 (or_1_out, opcode[0], opcode[1], opcode[2], opcode[3], opcode[4], opcode[5]);
  not not_2 (not_2_out, or_1_out);
  and and_1 (and_1_out, opcode[0], not_1_out);
  and and_2 (and_2_out, not_2_out, funct[0]);
  or or_2 (itIsUnsigned, and_1_out, and_2_out);
endmodule

module Load_Use_Hazard_Detector (
  input  [4:0] IFID_Ra,
  input  IDEX_MemRead,
  input  [4:0] IDEX_Rd,
  input  [4:0] IFID_Rb,
  output Load_Use_Hazard
);

  wire and_1_out, comparator_1_eq, comparator_2_eq, comparator_3_eq, not_1_out, or_1_out;
  wire [4:0] xor_1_out;

  Comparator #(.width(5)) comparator_1 (.a(IFID_Ra), .b(IDEX_Rd), .eq(comparator_1_eq));  // open: gt, lt
  Comparator #(.width(5)) comparator_2 (.a(IDEX_Rd), .b(IFID_Rb), .eq(comparator_2_eq));  // open: gt, lt
  assign xor_1_out = IDEX_Rd ^ IDEX_Rd;  // XOR_Gate xor_1, 5 bits wide
  or or_1 (or_1_out, comparator_1_eq, comparator_2_eq);
  not not_1 (not_1_out, comparator_3_eq);
  Comparator #(.width(5)) comparator_3 (.a(IDEX_Rd), .b(xor_1_out), .eq(comparator_3_eq));  // open: gt, lt
  and and_1 (and_1_out, IDEX_MemRead, or_1_out);
  and and_2 (Load_Use_Hazard, and_1_out, not_1_out);
endmodule

module Jump (
  input  [31:0] OriginalPC,
  input  [1:0] in_2,
  input  [31:0] Instruction,
  input  [31:0] Rs_IN,
  output [31:0] NewPC,
  output [4:0] rW
);

  wire and_1_out, not_1_out, not_2_out, not_3_out, not_4_out, not_5_out, or_1_out, or_2_out, or_3_out;

  or or_1 (or_1_out, Instruction[26], Instruction[27], Instruction[28], Instruction[29], Instruction[30], Instruction[31]);
  not not_1 (not_1_out, or_1_out);
  or or_2 (or_2_out, Instruction[31], Instruction[30], Instruction[29], Instruction[28], Instruction[27], Instruction[26]);
  not not_2 (not_2_out, Instruction[3]);
  not not_3 (not_3_out, Instruction[0]);
  not not_4 (not_4_out, or_2_out);
  or or_3 (or_3_out, Instruction[5], Instruction[4], not_2_out, Instruction[2], Instruction[1], not_3_out);
  not not_5 (not_5_out, or_3_out);
  Multiplexer #(.width(32), .enable("false")) multiplexer_1 (
    .in0({OriginalPC[31:28], Instruction[25:0], in_2}), .in1(Rs_IN), .out(NewPC), .sel(not_1_out));
  and and_1 (and_1_out, not_4_out, not_5_out);
  Multiplexer #(.width(5), .enable("false")) multiplexer_2 (
    .in0({5{1'b1}}), .in1(Instruction[15:11]), .out(rW), .sel(and_1_out));
endmodule

module Branch (
  input  [31:0] Instruction,
  input  [31:0] Rs,
  input  [31:0] Rt,
  output takeTheBranch,
  output [15:0] offset
);

  wire comparator_1_eq, comparator_2_gt, comparator_2_lt, multiplexer_1_out, multiplexer_2_out,
       multiplexer_3_out, multiplexer_4_out, not_1_out, not_2_out, not_3_out;

  Comparator #(.width(32)) comparator_1 (.a(Rs), .b(Rt), .eq(comparator_1_eq));  // open: gt, lt
  Comparator #(.width(32)) comparator_2 (
    .a(Rs), .b({32{1'b0}}), .gt(comparator_2_gt), .lt(comparator_2_lt));  // open: eq
  not not_1 (not_1_out, comparator_1_eq);
  not not_2 (not_2_out, comparator_2_gt);
  not not_3 (not_3_out, comparator_2_lt);
  Multiplexer #(.enable("false")) multiplexer_1 (
    .in0(not_2_out), .in1(comparator_2_gt), .out(multiplexer_1_out), .sel(Instruction[26]));
  Multiplexer #(.enable("false")) multiplexer_2 (
    .in0(comparator_2_lt), .in1(not_3_out), .out(multiplexer_2_out), .sel(Instruction[16]));
  Multiplexer #(.enable("false")) multiplexer_3 (
    .in0(comparator_1_eq), .in1(not_1_out), .out(multiplexer_3_out), .sel(Instruction[26]));
  Multiplexer #(.enable("false")) multiplexer_4 (
    .in0(multiplexer_3_out), .in1(multiplexer_1_out), .out(multiplexer_4_out), .sel(Instruction[27]));
  Multiplexer #(.enable("false")) multiplexer_5 (
    .in0(multiplexer_2_out), .in1(multiplexer_4_out), .out(takeTheBranch), .sel(Instruction[28]));

  assign offset = Instruction[15:0];
endmodule

module isBranchingOrNot (
  input  [5:0] sixBitOpcode,
  output isBranching
);

  wire and_1_out, and_2_out, not_1_out, not_2_out, not_3_out, not_4_out, not_5_out, not_6_out, not_7_out;

  not not_1 (not_1_out, sixBitOpcode[5]);
  not not_2 (not_2_out, sixBitOpcode[4]);
  not not_3 (not_3_out, sixBitOpcode[3]);
  not not_4 (not_4_out, sixBitOpcode[1]);
  not not_5 (not_5_out, sixBitOpcode[5]);
  not not_6 (not_6_out, sixBitOpcode[4]);
  not not_7 (not_7_out, sixBitOpcode[3]);
  and and_1 (and_1_out, not_1_out, not_2_out, not_3_out, not_4_out, sixBitOpcode[0]);
  and and_2 (and_2_out, not_5_out, not_6_out, not_7_out, sixBitOpcode[2]);
  or or_1 (isBranching, and_1_out, and_2_out);
endmodule

module isLoad (
  input  [5:0] opcode,
  output isLoad
);

  wire and_1_out, and_2_out, not_1_out, not_2_out, not_3_out, not_4_out, not_5_out, not_6_out;

  not not_1 (not_1_out, opcode[4]);
  not not_2 (not_2_out, opcode[3]);
  not not_3 (not_3_out, opcode[1]);
  not not_4 (not_4_out, opcode[4]);
  not not_5 (not_5_out, opcode[3]);
  not not_6 (not_6_out, opcode[2]);
  and and_1 (and_1_out, opcode[5], not_1_out, not_2_out, not_3_out);
  and and_2 (and_2_out, opcode[5], not_4_out, not_5_out, not_6_out, opcode[0]);
  or or_1 (isLoad, and_1_out, and_2_out);
endmodule

module isStore1 (
  input  [5:0] opcode,
  output isStore
);

  wire and_1_out, and_2_out, not_1_out, not_2_out, not_3_out, not_4_out, not_5_out;

  not not_1 (not_1_out, opcode[4]);
  not not_2 (not_2_out, opcode[2]);
  not not_3 (not_3_out, opcode[1]);
  not not_4 (not_4_out, opcode[4]);
  not not_5 (not_5_out, opcode[2]);
  and and_1 (and_1_out, opcode[5], not_1_out, opcode[3], not_2_out, not_3_out);
  and and_2 (and_2_out, opcode[5], not_4_out, opcode[3], not_5_out, opcode[0]);
  or or_1 (isStore, and_1_out, and_2_out);
endmodule

module isJorJR (
  input  [5:0] opcode,
  input  [5:0] funct,
  output JorJR
);

  wire and_1_out, not_1_out, not_2_out, not_3_out, not_4_out, not_5_out, or_1_out, or_2_out, or_3_out;

  not not_1 (not_1_out, opcode[1]);
  not not_2 (not_2_out, funct[3]);
  not not_3 (not_3_out, or_1_out);
  or or_1 (or_1_out, opcode[5], opcode[4], opcode[3], opcode[2], not_1_out, opcode[0]);
  or or_2 (or_2_out, opcode[5], opcode[4], opcode[3], opcode[2], opcode[1], opcode[0]);
  not not_4 (not_4_out, or_2_out);
  or or_3 (or_3_out, funct[5], funct[4], not_2_out, funct[2], funct[1], funct[0]);
  not not_5 (not_5_out, or_3_out);
  and and_1 (and_1_out, not_4_out, not_5_out);
  or or_4 (JorJR, not_3_out, and_1_out);
endmodule

module isJALorJALR (
  input  [5:0] opcode,
  input  [5:0] funct,
  output JALorJALR
);

  wire and_1_out, not_1_out, not_2_out, not_3_out, not_4_out, not_5_out, not_6_out, not_7_out, or_1_out,
       or_2_out, or_3_out;

  not not_1 (not_1_out, opcode[1]);
  not not_2 (not_2_out, opcode[0]);
  not not_3 (not_3_out, funct[3]);
  not not_4 (not_4_out, funct[0]);
  not not_5 (not_5_out, or_1_out);
  or or_1 (or_1_out, opcode[5], opcode[4], opcode[3], opcode[2], not_1_out, not_2_out);
  not not_6 (not_6_out, or_2_out);
  or or_2 (or_2_out, opcode[5], opcode[4], opcode[3], opcode[2], opcode[1], opcode[0]);
  or or_3 (or_3_out, funct[5], funct[4], not_3_out, funct[2], funct[1], not_4_out);
  not not_7 (not_7_out, or_3_out);
  and and_1 (and_1_out, not_6_out, not_7_out);
  or or_4 (JALorJALR, not_5_out, and_1_out);
endmodule

module RightShift2 (
  input  [31:0] B,
  input  Cin,
  output [31:0] Bout
);


  assign Bout = {{2{Cin}}, B[31:2]};
endmodule

module isBEQorBNE (
  input  [5:0] opode,
  output isBNEorBEQ
);

  wire not_1_out, not_2_out, not_3_out, not_4_out, not_5_out, or_1_out, or_2_out;

  not not_1 (not_1_out, opode[2]);
  not not_2 (not_2_out, opode[2]);
  not not_3 (not_3_out, opode[0]);
  not not_4 (not_4_out, or_1_out);
  or or_1 (or_1_out, opode[5], opode[4], opode[3], not_1_out, opode[1], opode[0]);
  not not_5 (not_5_out, or_2_out);
  or or_2 (or_2_out, opode[5], opode[4], opode[3], not_2_out, opode[1], not_3_out);
  or or_3 (isBNEorBEQ, not_4_out, not_5_out);
endmodule

module forwardRA (
  input  [4:0] rW_WB,
  input  isJALorJALR_WB,
  input  [4:0] rW_MEM,
  input  isJALorJALR_MEM,
  input  [31:0] instruction,
  output [1:0] forwardFrom
);

  wire and_1_out, and_2_out, comparator_1_eq, comparator_2_eq, not_1_out, not_2_out, not_3_out, not_4_out,
       not_5_out, not_6_out, not_7_out, or_1_out, or_2_out, or_3_out, or_4_out, or_5_out;

  not not_1 (not_1_out, instruction[3]);
  not not_2 (not_2_out, instruction[3]);
  not not_3 (not_3_out, instruction[0]);
  Comparator #(.width(5)) comparator_1 (.a(rW_WB), .b(instruction[25:21]), .eq(comparator_1_eq));  // open: gt, lt
  not not_4 (not_4_out, or_1_out);
  or or_1 (or_1_out, instruction[31], instruction[30], instruction[29], instruction[28], instruction[27], instruction[26]);
  not not_5 (not_5_out, or_2_out);
  or or_2 (or_2_out, instruction[5], instruction[4], not_1_out, instruction[2], instruction[1], instruction[0]);
  or or_3 (or_3_out, instruction[31], instruction[30], instruction[29], instruction[28], instruction[27], instruction[26]);
  not not_6 (not_6_out, or_3_out);
  or or_4 (or_4_out, instruction[5], instruction[4], not_2_out, instruction[2], instruction[1], not_3_out);
  Comparator #(.width(5)) comparator_2 (.a(rW_MEM), .b(instruction[25:21]), .eq(comparator_2_eq));  // open: gt, lt
  not not_7 (not_7_out, or_4_out);
  and and_1 (and_1_out, not_4_out, not_5_out);
  and and_2 (and_2_out, not_6_out, not_7_out);
  or or_5 (or_5_out, and_1_out, and_2_out);
  and and_3 (forwardFrom[1], comparator_1_eq, isJALorJALR_WB, or_5_out);
  and and_4 (forwardFrom[0], comparator_2_eq, isJALorJALR_MEM, or_5_out);
endmodule
